// Logisim project gate_nand.circ as structural Verilog: 1 circuit, main circuit main
module main (
  input  A,
  input  B,
  output Output
);

  nand NAND (Output, A, B);

  // Notes on the sheet:
  //   NAND Gate
  //   A  B  Ouput
  //   0  0       1
  //   0  1       1
  //   1  0       1
  //   1  1       0
endmodule
