// Logisim project half_adder.circ as structural Verilog: 2 circuits, main circuit main
// HA
module main (
  input  A,
  input  A_2,
  input  B,
  input  B_2,
  output Sum,
  output Sum_2,
  output C_Out,
  output C_Out_2
);

  wire nand_1_out;

  xor xor_1 (Sum, A, B);
  and and_1 (C_Out, A, B);
  xor xor_2 (Sum_2, A_2, B_2);
  nand nand_1 (nand_1_out, A_2, B_2);
  not not_1 (C_Out_2, nand_1_out);

  // Notes on the sheet:
  //   Half-Adder
  //   A   B   Sum   C_Out
  //   0   0      0        0
  //   0   1      1        0
  //   1   0      1        0
  //   1   1      0        1
endmodule

module half_adder (
);

  main main_1 ();  // open: A, A_2, B, B_2, Sum, Sum_2, C_Out, C_Out_2
endmodule
